# Fritzing sketch Sterownik (saved by Fritzing 0.9.3b)
circuit board: 9.48578cm x 7.16401cm
breadboards: 1

parts:
  Q1 = Basic FET N-Channel [package="TO220 [THT]"]
  U1 = atmega328 [package=dip]
  Q2 = Basic FET N-Channel [package="TO220 [THT]"]
  Q3 = Basic FET N-Channel [package="TO220 [THT]"]
  Q4 = Basic FET P-Channel [package="TO220 [THT]"]
  Q5 = Basic FET P-Channel [package="TO220 [THT]"]
  Q6 = Basic FET P-Channel [package="TO220 [THT]"]
  Q7 = Basic FET P-Channel [package="TO220 [THT]"]
  Q8 = Basic FET P-Channel [package="TO220 [THT]"]
  Q9 = Basic FET P-Channel [package="TO220 [THT]"]
  XTAL1 = Crystal [frequency="16 Mhz" package=THT]
  J10 = female pin header, 4 pins [form="♀ (female)"]
  J11 = female pin header, 4 pins [form="♀ (female)"]
  J12 = female pin header, 4 pins [form="♀ (female)"]
  J13 = female pin header, 4 pins [form="♀ (female)"]
  J14 = female pin header, 4 pins [form="♀ (female)"]
  R1 = Resistor [tolerance=±5% resistance=220 package=THT]
  J15 = female pin header, 4 pins [form="♀ (female)"]
  Q10 = Basic FET P-Channel [package="TO220 [THT]"]
  J8 = female pin header, 4 pins [form="♀ (female)"]
  J9 = female pin header, 4 pins [form="♀ (female)"]
  Q11 = Basic FET P-Channel [package="TO220 [THT]"]
  C2 = Ceramic Capacitor [capacitance=100nF package="200 mil [THT, multilayer]"]
  C1 = Ceramic Capacitor [capacitance=100nF package="200 mil [THT, multilayer]"]
  D1 = Rectifier Diode [part_number=1N4001 package="300 mil [THT]"]
  F1 = Resettable Fuse PTC [package=ptc]
  Fuse1 = Fuse with Handler [part_number=Htc-15m]
  IC1 = ULN2003A [package="DIP16 [THT]"]
  R2 = Resistor [tolerance=±5% resistance=220 package=THT]
  Q12 = NPN-Transistor [package="TO92 [THT]"]
  R3 = Resistor [tolerance=±5% resistance=220 package=THT]
  R7 = Resistor [tolerance=±5% resistance=220 package=THT]
  R8 = Resistor [tolerance=±5% resistance=220 package=THT]
  R9 = Resistor [tolerance=±5% resistance=220 package=THT]
  R10 = Resistor [tolerance=±5% resistance=220 package=THT]
  R11 = Resistor [tolerance=±5% resistance=220 package=THT]
  R4 = Resistor [tolerance=±5% resistance=220 package=THT]
  R12 = Resistor [tolerance=±5% resistance=220 package=THT]

nets:
  N1: Q1.gate, U1.D11_(PWM)
  N2: Q1.drain, J10.pin2, J11.pin2, J12.pin2, J13.pin2, J14.pin2, J15.pin2, J9.pin2
  N3: Q1.source, U1.GND, Q2.source, Q3.source, J8.pin2, C2.1, C1.1, IC1.0V, Q12.E
  N4: U1.RESET, R1.Pin_0
  N5: U1.D0_(RX), D1.cathode
  N6: U1.D2, IC1.In_7
  N7: U1.D3_(PWM), R3.Pin_1
  N8: U1.D4, IC1.In_6
  N9: U1.VCC, U1.AVCC, R1.Pin_1, F1.2
  N10: U1.XLAT1, XTAL1.pin_0, C1.0
  N11: U1.XLAT2, XTAL1.pin_1, C2.0
  N12: U1.D5_(PWM), IC1.In_5
  N13: U1.D6_(PWM), IC1.In_4
  N14: U1.D7, IC1.In_3
  N15: U1.D8, IC1.In_2
  N16: U1.D9_(PWM), Q3.gate
  N17: U1.D10_(PWM), Q2.gate
  N18: U1.D12, IC1.In_1
  N19: Q2.drain, J10.pin3, J11.pin3, J12.pin3, J13.pin3, J14.pin3, J15.pin3, J9.pin3
  N20: Q3.drain, J10.pin4, J11.pin4, J12.pin4, J13.pin4, J14.pin4, J15.pin4, J9.pin4
  N21: Q4.gate, R4.Pin_1
  N22: Q4.drain, J9.pin1
  N23: Q4.source, Q5.source, Q6.source, Q7.source, Q8.source, Q9.source, Q10.source, Q11.drain, IC1.Out_7, IC1.Out_6, IC1.Out_5, IC1.Out_4, IC1.Out_3, IC1.Out_1, R7.Pin_0, R8.Pin_0, R9.Pin_0, R10.Pin_0, R11.Pin_0, R4.Pin_0, R12.Pin_1
  N24: Q5.gate, R11.Pin_1
  N25: Q5.drain, J14.pin1
  N26: Q6.gate, R7.Pin_1
  N27: Q6.drain, J10.pin1
  N28: Q7.gate, R8.Pin_1
  N29: Q7.drain, J11.pin1
  N30: Q8.gate, R9.Pin_1
  N31: Q8.drain, J12.pin1
  N32: Q9.gate, R10.Pin_1
  N33: Q9.drain, J13.pin1
  N34: J15.pin1, Q10.drain
  N35: Q10.gate, IC1.Out_2, R12.Pin_0
  N36: J8.pin1, Fuse1.Connector2
  N37: J8.pin3, F1.1
  N38: J8.pin4, D1.anode
  N39: Q11.gate, R2.Pin_0, Q12.C
  N40: Q11.source, Fuse1.Connector1, R2.Pin_1
  N41: Q12.B, R3.Pin_0
