# Fritzing sketch Brama 1.0 (saved by Fritzing 0.9.2b)
breadboards: 5

parts:
  Part1 = Arduino Uno (Rev3)
  U1 = ESP8266 WiFi Module [part_number=ESP8266]
  R1 = Resistor [tolerance=±5% resistance=4.7k package=THT]
  R2 = Resistor [tolerance=±5% resistance=470 package=THT]
  U2 = RF-LINK_RX [package=rf-link_rx]
  U4 = atmega328 [package=dip]
  XTAL1 = Crystal [frequency="16 Mhz" package=THT]
  U3 = atmega328 [package=dip]
  C5 = Capacitor [package=cap-pth-small2]
  C6 = Capacitor [package=cap-pth-small2]
  C7 = Capacitor [package=cap-pth-small2]
  C8 = Capacitor [package=cap-pth-small2]
  XTAL2 = Crystal [frequency="16 Mhz" package=THT]
  U5 = RF-LINK_TX [package=rf-link_tx]
  U6 = RF-LINK_TX [package=rf-link_tx]
  S1 = Round Pushbutton
  S2 = Round Pushbutton
  S3 = Round Pushbutton
  S4 = Round Pushbutton
  S5 = Round Pushbutton
  S6 = Round Pushbutton
  KY-1 = Keyes Relay [package=THT]
  KY-2 = Keyes Relay [package=THT]
  J1 = Screw terminal - 2 pins [package=THT]
  M1 = DC Motor
  KY-3 = Keyes Relay [package=THT]
  KY-4 = Keyes Relay [package=THT]
  S7 = SWITCH-MOMENTARY-2 [package=tactile-pth-12mm]
  S8 = SWITCH-MOMENTARY-2 [package=tactile-pth-12mm]
  J2 = screw terminal, 2 pins  # not connected
  J3 = screw terminal, 3 pins  # not connected
  R3 = Resistor [tolerance=±5% resistance=330 package=THT]
  R4 = Resistor [tolerance=±5% resistance=330 package=THT]

nets:
  N1: Part1.D9_PWM, S8.2
  N2: Part1.D13/SCK, U2.Data#3
  N3: Part1.D2, U1.RXD
  N4: Part1.D3_PWM, R1.Pin_1
  N5: Part1.D6_PWM, KY-3.signal, KY-4.signal
  N6: Part1.D7, KY-1.signal, KY-2.signal
  3V3: Part1.3V3, U1.VCC, U1.RST, U1.CH_PD, U1.TXD, R1.Pin_0, R2.Pin_1
  5V: Part1.5V, U2.VCC, KY-1.power, KY-2.power, KY-3.power, KY-4.power, R3.Pin_1, R4.Pin_1
  GND: Part1.GND, U1.GND, R2.Pin_0, U2.GND, KY-1.ground, KY-2.ground, KY-3.ground, KY-4.ground
  VCC: U4.VCC, U4.AVCC, U6.+5V
  GND_2: U4.GND, C7.1, C8.2, U6.GND
  N7: U4.XLAT1, C7.2, XTAL2.pin_0
  N8: U4.XLAT2, C8.1, XTAL2.pin_1
  N9: U4.D9_(PWM), S5.leg0
  N10: U4.D10_(PWM), S6.leg0
  N11: U4.D11_(PWM), S4.leg0
  N12: U4.D12, U6.DATA
  N13: XTAL1.pin_0, U3.XLAT1, C5.2
  N14: XTAL1.pin_1, U3.XLAT2, C6.1
  VCC_2: U3.VCC, U3.AVCC, U5.+5V
  GND_3: U3.GND, C5.1, C6.2, U5.GND
  N15: U3.D9_(PWM), S2.leg0
  N16: U3.D10_(PWM), S1.leg0
  N17: U3.D11_(PWM), S3.leg0
  N18: U3.D12, U5.DATA
  N19: S1.leg1, S2.leg1, S3.leg1
  N20: S4.leg1, S5.leg1, S6.leg1
  N21: KY-1.NC, M1.pin_1, KY-3.NC
  N22: KY-1.C, J1.pin1, KY-4.C
  N23: KY-2.NC, M1.pin_2, KY-4.NC
  N24: KY-2.C, J1.pin2, KY-3.C
  N25: S7.1, S8.1

notes:
  oodbiornik radiowy, pilota
  Moduł wifi do urządzeń
  nadających na wifi
  Nadajnik pilota radiowego
  Bezpiecznik
  10A
  230V
  AV
  Krańcówka
  IR LED
  czujnik przerwania wiązki LED

custom parts:
  ESP8266 WiFi Module: Generic WiFi Module based on the ESP8266 with onboard PCB antenna and UART communications
  RF-LINK_RX: RF Link receivers- WRL-8947, 8948, 8949, 8950
  RF-LINK_TX: Common RF transmitter of the 315.00Mhz varity
  Keyes Relay: The Keyes 5V relay module is suitable for SCM development, home appliance control. It uses a 5V~12V TIL control signal which can control DC / AC signal.
