# Fritzing sketch Brama 2.0 (saved by Fritzing 0.9.2b)
circuit board: 16.968cm x 7.54076cm
breadboards: 1

parts:
  U1 = atmega328 [package=dip]
  C1 = Ceramic Capacitor [capacitance=22µF package="0603 [SMD, multilayer]"]
  C1_2 = Ceramic Capacitor [capacitance=22µF package="200 mil [THT, multilayer]"]
  S1 = Pushbutton [package="[THT]"]
  J1 = female pin header, 2 pins [form="♀ (female)"]
  S2 = Pushbutton [package=THT]
  S3 = Pushbutton [package=THT]
  IR1 = TSOP312.., 314.. [package=THT]
  D1 = LTE-302 [package=lte-302]
  R1 = Resistor [tolerance=±5% resistance=220 package=THT]
  XTAL1 = Crystal [frequency="16 Mhz" package=THT]
  U2 = ESP8266 WiFi Module [part_number=ESP8266]
  R2 = Resistor [tolerance=±5% resistance=10k package=THT]
  C2 = Electrolytic Capacitor [capacitance=10µF package="100 mil [THT, electrolytic]"]
  R3 = Resistor [tolerance=±5% resistance=4.7k package=THT]
  R4 = Resistor [tolerance=±5% resistance=10k package=THT]
  KY-1 = Keyes Relay [package=THT]
  KY-2 = Keyes Relay [package=THT]
  NRF24L1 = NRF24L01
  C3 = Electrolytic Capacitor [capacitance=1µF package="100 mil [THT, electrolytic]"]
  C4 = Electrolytic Capacitor [capacitance=1µF package="100 mil [THT, electrolytic]"]
  C5 = Ceramic Capacitor [capacitance=100nF package="100 mil [THT, multilayer]"]
  C6 = Ceramic Capacitor [capacitance=100nF package="100 mil [THT, multilayer]"]
  C7 = Ceramic Capacitor [capacitance=100nF package="100 mil [THT, multilayer]"]
  C8 = Ceramic Capacitor [capacitance=100nF package="100 mil [THT, multilayer]"]
  C9 = Electrolytic Capacitor [capacitance=1µF package="100 mil [THT, electrolytic]"]
  C10 = Ceramic Capacitor [capacitance=100nF package="100 mil [THT, multilayer]"]
  R5 = Trimmer Potentiometer [maximum_resistance=10kΩ package=THT]
  S4 = Pushbutton [package="[THT]"]
  S5 = Pushbutton [package="[THT]"]
  S6 = Pushbutton [package="[THT]"]
  U3 = Voltage Regulator [package=to220-adj]
  Power_plug1 = Power plug
  C11 = Ceramic Capacitor [capacitance=100nF package="100 mil [THT, multilayer]"]
  R6 = Resistor [tolerance=±5% resistance=330 package=THT]
  C12 = Electrolytic Capacitor [capacitance=1µF package="100 mil [THT, electrolytic]"]
  C13 = Electrolytic Capacitor [capacitance=1µF package="100 mil [THT, electrolytic]"]
  R7 = Resistor [tolerance=±5% resistance=560 package=THT]
  R8 = Resistor [tolerance=±5% resistance=47 package=THT]
  C14 = Capacitor [package=cap-pth-small-kit]
  L1 = Inductor [package="400 mil [THT]"]

nets:
  GND: U1.RESET, U1.GND, C1_2.1, S1.Pin_1, S1.Pin_2, S1.Pin_3, S1.Pin_4, S2.leg1, S3.leg0, IR1.GND, D1.A, U2.GND, C2.-, R4.Pin_1, NRF24L1.GND, C3.-, C4.+, C5.0, C6.0, C7.1, C8.1, R5.leg2, S4.Pin_3, S4.Pin_4, S5.Pin_3, S5.Pin_4, S6.Pin_3, S6.Pin_4, Power_plug1.GND, C11.1, C12.-, C13.-, R8.Pin_1
  N1: U1.D0_(RX), J1.pin1
  N2: U1.D1_(TX), J1.pin2
  N3: U1.D2, S2.leg0
  N4: U1.D3_(PWM), S3.leg1
  N5: U1.D4, IR1.Data
  N6: U1.VCC, U1.AVCC, IR1.Vs, R1.Pin_0, KY-1.power, KY-2.power, C4.-, C5.1, C6.1, C7.0, R5.leg1
  N7: U1.XLAT1, C1.1, XTAL1.pin_0
  N8: U1.XLAT2, C1_2.0, XTAL1.pin_1
  N9: U1.D5_(PWM), U2.TXD
  N10: U1.D6_(PWM), R3.Pin_0, C9.-, C10.0
  N11: U1.D7, KY-1.signal
  N12: U1.D8, KY-2.signal
  N13: U1.D9_(PWM), NRF24L1.CE
  N14: U1.D10_(PWM), NRF24L1.CSN
  N15: U1.D11_(PWM), NRF24L1.MOSI
  N16: U1.D12, NRF24L1.MISO
  N17: U1.D13, NRF24L1.SCK
  N18: U1.A0, R5.wiper
  N19: U1.A3, S6.Pin_1, S6.Pin_2
  N20: U1.A4, S5.Pin_1, S5.Pin_2
  N21: U1.A5, S4.Pin_1, S4.Pin_2
  N22: D1.C, R1.Pin_1
  N23: U2.RXD, R3.Pin_1, R4.Pin_0, C9.+, C10.1
  N24: U2.CH_PD, R2.Pin_1
  N25: R2.Pin_0, C2.+, NRF24L1.VCC, C3.+, C8.0, U3.IN, R6.Pin_1
  N26: KY-1.ground, KY-2.ground
  N27: U3.ADJ, R6.Pin_0, C12.+, C13.+
  N28: U3.OUT, Power_plug1.VCC, C11.0
  N29: R7.Pin_1, R8.Pin_0
  N30: C14.1, L1.pin_0
  N31: C14.2, L1.pin_1

notes:
  Konwerter
  UART
  Krańcówka L
  Krańcówka R
  Czujnik przerwania wiązki IR (w przyszłości)
  LM317 V out: 3,6V

custom parts:
  ESP8266 WiFi Module: Generic WiFi Module based on the ESP8266 with onboard PCB antenna and UART communications
  Keyes Relay: The Keyes 5V relay module is suitable for SCM development, home appliance control. It uses a 5V~12V TIL control signal which can control DC / AC signal.
  NRF24L01: NRF24L01 module
