# Fritzing sketch Pcb (saved by Fritzing 0.9.2b)
circuit board: 11.0827cm x 12.1015cm
breadboards: 1

parts:
  U1 = atmega328 [package=dip]
  S1 = Momentary Switch [package=ksa_sealed_tac_switch]
  XTAL1 = Crystal [frequency="16 Mhz" package=THT]
  C1 = Ceramic Capacitor [capacitance=100nF package="100 mil [THT, multilayer]"]
  C2 = Ceramic Capacitor [capacitance=100nF package="100 mil [THT, multilayer]"]
  U2 = ESP8266 WiFi Module [part_number=ESP8266]
  R2 = Resistor [tolerance=±5% resistance=220 package=THT]
  R3 = Resistor [tolerance=±5% resistance=220 package=THT]
  R4 = Resistor [tolerance=±5% resistance=220 package=THT]
  C3 = Ceramic Capacitor [capacitance=100nF package="100 mil [THT, multilayer]"]
  S2 = Pushbutton [package="[THT]"]
  U3 = Voltage Regulator - Variable [package="TO220 [THT]"]
  R5 = Resistor [tolerance=±5% resistance=220 package=THT]
  C5 = Electrolytic Capacitor [capacitance=1µF package="100 mil [THT, electrolytic]"]
  R6 = Resistor [tolerance=±5% resistance=220 package=THT]
  C6 = Electrolytic Capacitor [capacitance=1µF package="100 mil [THT, electrolytic]"]
  C7 = Ceramic Capacitor [capacitance=100nF package="100 mil [THT, multilayer]"]
  C8 = Electrolytic Capacitor [capacitance=1µF package="100 mil [THT, electrolytic]"]
  C9 = Ceramic Capacitor [capacitance=100nF package="100 mil [THT, multilayer]"]
  S3 = Toggle Switch [package=THT]
  L1 = Inductor [package="400 mil [THT]"]
  R1 = Trimmer Potentiometer [maximum_resistance=10kΩ package=THT]
  D1 = Rectifier Diode [part_number=1N4001 package="300 mil [THT]"]
  Pad1 = Pad [width=4 height=4 connect=center]
  Pad2 = Pad [width=4 height=4 connect=center]

nets:
  N1: U1.RESET, S1.2
  GND: U1.GND, S1.3, C1.1, C2.1, U2.RST, U2.GND, R3.Pin_0, S2.Pin_3, S2.Pin_4, R5.Pin_0, C5.-, C6.-, C7.0, C8.-, C9.1, S3.L1, R1.leg2, Pad2.pad
  N2: U1.XLAT1, XTAL1.pin_0, C1.0
  N3: U1.XLAT2, XTAL1.pin_1, C2.0
  N4: U1.D5_(PWM), R2.Pin_0
  N5: U1.D6_(PWM), U2.TXD, C3.0, C3.1, L1.pin_0, L1.pin_1
  N6: U1.AVCC, U3.IN, C7.1, C8.+, C9.0, R1.leg1
  N7: U1.A0, R1.wiper
  N8: U1.A5, S3.L2
  N9: U2.RXD, R2.Pin_1, R3.Pin_1
  N10: U2.VCC, R4.Pin_0, U3.OUT
  N11: U2.CH_PD, R4.Pin_1
  N12: U3.ADJ, R5.Pin_1, R6.Pin_0, C6.+
  N13: C5.+, R6.Pin_1
  N14: D1.cathode, Pad1.pad

custom parts:
  ESP8266 WiFi Module: Generic WiFi Module based on the ESP8266 with onboard PCB antenna and UART communications
