# Fritzing sketch Nadajnik pcb 2 smd (saved by Fritzing 0.9.3b)
circuit board: 2.685cm x 4.24289cm
breadboards: 1

parts:
  U1 = ATMEGA168 [package=tqfp]
  S1 = Pushbutton [package="[THT]"]
  S2 = Pushbutton [package="[THT]"]

nets:
  N1: U1.GND, U1.AGND, S1.Pin_3, S1.Pin_4
  N2: U1.VCC, U1.AVCC
  N3: S1.Pin_1, S1.Pin_2, S2.Pin_3, S2.Pin_4
