# Fritzing sketch Nadajnik pcb 2 (saved by Fritzing 0.9.2b)
circuit board: 5.60317cm x 8.98783cm
breadboards: 1

parts:
  U1 = Voltage Regulator [package=to220-adj]
  U2 = atmega328 [package=dip]
  S1 = Pushbutton [package="[THT]"]
  S2 = Pushbutton [package="[THT]"]
  S3 = Pushbutton [package="[THT]"]
  R1 = Resistor [tolerance=±5% resistance=220 package=THT]
  R2 = Resistor [tolerance=±5% resistance=220 package=THT]
  C1 = Ceramic Capacitor [capacitance=100nF package="100 mil [THT, multilayer]"]
  C2 = Electrolytic Capacitor [capacitance=1µF package="100 mil [THT, electrolytic]"]
  R3 = Resistor [tolerance=±5% resistance=220 package=THT]
  R4 = Resistor [tolerance=±5% resistance=220 package=THT]
  R5 = Resistor [tolerance=±5% resistance=220 package=THT]
  LED1 = LED - 5mm [color="Red (633nm)" package="5 mm [THT]"]
  LED2 = LED - 5mm [color="Red (633nm)" package="5 mm [THT]"]
  LED3 = LED - 5mm [color="Red (633nm)" package="5 mm [THT]"]
  U3 = Voltage Regulator [package=to220-adj]
  R6 = Resistor [tolerance=±5% resistance=220 package=THT]
  R7 = Resistor [tolerance=±5% resistance=220 package=THT]
  C3 = Electrolytic Capacitor [capacitance=1µF package="100 mil [THT, electrolytic]"]
  D1 = Rectifier Diode [part_number=1N4001 package="300 mil [THT]"]
  XTAL1 = Crystal [frequency="16 Mhz" package=THT]
  C5 = Ceramic Capacitor [capacitance=100nF package="200 mil [THT, multilayer]"]
  C4 = Ceramic Capacitor [capacitance=100nF package="200 mil [THT, multilayer]"]
  C6 = Ceramic Capacitor [capacitance=100nF package="100 mil [THT, multilayer]"]

nets:
  N1: U1.ADJ, R1.Pin_0, R2.Pin_1, R4.Pin_1
  N2: U1.IN, C1.0, U3.IN, D1.cathode, C6.0
  N3: U2.D2, S1.Pin_3
  N4: U2.D3_(PWM), S2.Pin_3, S2.Pin_4
  N5: U2.D4, S3.Pin_3, S3.Pin_4
  N6: U2.VCC, U2.AVCC, C2.+
  N7: U2.GND, S1.Pin_1, S1.Pin_2, S2.Pin_1, S2.Pin_2, S3.Pin_1, R5.Pin_0, R7.Pin_0, C3.-, C5.1, C4.1, C6.1
  N8: U2.XLAT1, XTAL1.pin_0, C4.0
  N9: U2.XLAT2, XTAL1.pin_1, C5.0
  N10: U2.A3, LED3.anode
  N11: U2.A4, LED2.anode
  N12: U2.A5, LED1.anode
  N13: R2.Pin_0, C1.1, R3.Pin_1
  N14: R3.Pin_0, LED1.cathode
  N15: R4.Pin_0, LED2.cathode
  N16: R5.Pin_1, LED3.cathode
  N17: U3.ADJ, R6.Pin_0, R7.Pin_1
  N18: U3.OUT, R6.Pin_1, C3.+, D1.anode
