# Fritzing sketch Nadajnik pcb 3 smd (saved by Fritzing 0.9.3b)
circuit board: 3.3cm x 7cm
breadboards: 1

parts:
  U1 = ATMEGA168 [package=tqfp]
  C1 = Ceramic Capacitor [capacitance=100nF package="0805 [SMD, multilayer]"]
  D1 = Rectifier Diode [part_number=1N4001 package="300 mil [THT]"]

nets:
  N1: U1.GND, U1.AGND, C1.1
  N2: U1.VCC, U1.AVCC, C1.0, D1.cathode
