# Fritzing sketch Mikrokontroler PCB (saved by Fritzing 0.9.3b)
circuit board: 14.1455cm x 18.1841cm
breadboards: 1

parts:
  U1 = atmega328 [package=dip]
  XTAL1 = Crystal [frequency="16 Mhz" package=THT]
  C1 = Ceramic Capacitor [capacitance=100nF package="100 mil [THT, multilayer]"]
  C2 = Ceramic Capacitor [capacitance=100nF package="100 mil [THT, multilayer]"]
  U2 = ESP8266 WiFi Module [part_number=ESP8266]
  R2 = Resistor [tolerance=±5% resistance=220 package=THT]
  R3 = Resistor [tolerance=±5% resistance=220 package=THT]
  R4 = Resistor [tolerance=±5% resistance=220 package=THT]
  C3 = Ceramic Capacitor [capacitance=100nF package="100 mil [THT, multilayer]"]
  S2 = Pushbutton [package="[THT]"]
  C8 = Electrolytic Capacitor [capacitance=1µF package="100 mil [THT, electrolytic]"]
  C9 = Ceramic Capacitor [capacitance=100nF package="100 mil [THT, multilayer]"]
  S3 = Toggle Switch [package=THT]
  R1 = Trimmer Potentiometer [maximum_resistance=10kΩ package=THT]
  C10 = Electrolytic Capacitor [capacitance=1µF package="100 mil [THT, electrolytic]"]
  C11 = Ceramic Capacitor [capacitance=100nF package="100 mil [THT, multilayer]"]
  R7 = Resistor [tolerance=±5% resistance=220 package=THT]
  7805 = Voltage Regulator - 5V [package="TO220 [THT]"]
  C12 = Electrolytic Capacitor [capacitance=10µF package="200 mil [THT, electrolytic]"]
  lm217T = Basic FET P-Channel [package="TO220 [THT]"]
  C13 = Ceramic Capacitor [capacitance=100nF package="100 mil [THT, multilayer]"]
  R8 = Resistor [tolerance=±5% resistance=220 package=THT]
  R9 = Resistor [tolerance=±5% resistance=220 package=THT]
  D1 = Rectifier Diode [part_number=1N4001 package="300 mil [THT]"]
  D2 = Rectifier Diode [part_number=1N4001 package="300 mil [THT]"]
  C14 = Electrolytic Capacitor [capacitance=1µF package="100 mil [THT, electrolytic]"]
  C15 = Ceramic Capacitor [capacitance=100nF package="100 mil [THT, multilayer]"]
  C16 = Electrolytic Capacitor [capacitance=1µF package="200 mil [THT, electrolytic]"]
  D3 = Rectifier Diode [part_number=1N4001 package="300 mil [THT]"]
  D4 = Rectifier Diode [part_number=1N4001 package="300 mil [THT]"]
  D6 = Rectifier Diode [part_number=1N4001 package="300 mil [THT]"]
  R10 = Resistor [tolerance=±5% resistance=220 package=THT]
  R11 = Resistor [tolerance=±5% resistance=220 package=THT]
  R12 = Resistor [tolerance=±5% resistance=220 package=THT]
  C17 = Ceramic Capacitor [capacitance=100nF package="100 mil [THT, multilayer]"]
  Fuse1 = Fuse with Handler [part_number=Htc-15m]  # not connected

nets (from the pcb view):
  N1: U1.RESET, R10.Pin_1
  N2: U1.VCC, U1.AVCC, C8.+, C9.0, R1.leg1, lm217T.source, D2.anode, C15.1, R10.Pin_0, R11.Pin_1, R12.Pin_1
  GND: U1.GND, C1.1, C2.1, U2.GND, R3.Pin_0, S2.Pin_1, S2.Pin_2, C8.-, C9.1, S3.COM, R1.leg2, C10.-, C11.1, 7805.GND, C12.+, C13.1, R8.Pin_0, C16.-
  N3: U1.XLAT1, XTAL1.pin_0, C1.0
  N4: U1.XLAT2, XTAL1.pin_1, C2.0
  N5: U1.D5_(PWM), R2.Pin_0, C17.0
  N6: U1.D6_(PWM), U2.TXD, C3.0, C3.1
  N7: U1.A0, R1.wiper
  N8: U1.A5, S3.L2
  N9: U2.RXD, R2.Pin_1, R3.Pin_1, C17.1
  N10: U2.VCC, R4.Pin_0, C10.+, C11.0, R7.Pin_0, C12.-, lm217T.drain, R9.Pin_1, D1.anode, D2.cathode, C14.+
  N11: U2.RST, S2.Pin_3, S2.Pin_4, R7.Pin_1
  N12: U2.CH_PD, R4.Pin_1
  N13: 7805.input_voltage, C13.0, C16.+, D4.cathode, D6.cathode
  N14: lm217T.gate, R8.Pin_1, R9.Pin_0, D1.cathode, C14.-, C15.0
  N15: D3.cathode, D4.anode

notes:
  Transformator 70061K

custom parts:
  ESP8266 WiFi Module: Generic WiFi Module based on the ESP8266 with onboard PCB antenna and UART communications
