# Fritzing sketch Mikrokontroler PCB góra (saved by Fritzing 0.9.3b)
circuit board: 15.6144cm x 6.13307cm
breadboards: 1

parts:
  J32 = female pin header, 5 pins [form="♀ (female)"]
  J31 = female pin header, 7 pins [form="♀ (female)"]
  Q1 = npn-Powertransistor [package="TO220 [THT]"]
  Q2 = npn-Powertransistor [package="TO220 [THT]"]
  Q3 = npn-Powertransistor [package="TO220 [THT]"]
  Q4 = npn-Powertransistor [package="TO220 [THT]"]
  Q5 = npn-Powertransistor [package="TO220 [THT]"]
  R1 = TRIMPOT [package=3362u-2]
  R2 = TRIMPOT [package=3362u-2]
  R3 = TRIMPOT [package=3362u-2]
  R4 = TRIMPOT [package=3362u-2]
  R5 = TRIMPOT [package=3362u-2]
  R6 = TRIMPOT [package=3362u-2]
  Q6 = NPN-Transistor [package="TO92 [THT]"]
  R7 = Resistor [tolerance=±5% resistance=220 package=THT]
  Q7 = NPN-Transistor [package="TO92 [THT]"]
  J29 = female pin header, 6 pins [form="♀ (female)"]
  R8 = Resistor [tolerance=±5% resistance=220 package=THT]
  Q9 = NPN-Transistor [package="TO92 [THT]"]
  Q10 = NPN-Transistor [package="TO92 [THT]"]
  R10 = Resistor [tolerance=±5% resistance=220 package=THT]
  R11 = Resistor [tolerance=±5% resistance=220 package=THT]
  Q11 = NPN-Transistor [package="TO92 [THT]"]
  R12 = Resistor [tolerance=±5% resistance=220 package=THT]
  Q12 = NPN-Transistor [package="TO92 [THT]"]
  R13 = Resistor [tolerance=±5% resistance=220 package=THT]
  Q13 = NPN-Transistor [package="TO92 [THT]"]
  R14 = Resistor [tolerance=±5% resistance=220 package=THT]
  Q14 = NPN-Transistor [package="TO92 [THT]"]
  R15 = Resistor [tolerance=±5% resistance=220 package=THT]
  J28 = female pin header, 3 pins [form="♀ (female)"]
  J33 = female pin header, 4 pins [form="♀ (female)"]  # not connected
  J33_2 = male pin header, 4 pins [form="♂ (male)"]
  J34 = female pin header, 3 pins [form="♀ (female)"]
  J35 = female pin header, 3 pins [form="♀ (female)"]

nets:
  N1: J32.pin1, J31.pin1
  N2: J32.pin2, J31.pin2
  N3: J32.pin3, J31.pin3
  N4: J32.pin4, J31.pin4
  N5: J32.pin5, J31.pin5
  N6: J31.pin6, J29.pin2
  N7: J31.pin7, R1.CW, R2.CW, R3.CW, R4.CW, R5.CW, R6.CW, J29.pin3
  N8: Q1.base, Q10.C
  N9: Q1.collector, Q2.collector, Q3.collector, Q4.collector, Q5.collector
  N10: Q2.base, Q13.C, Q14.C
  N11: Q3.base, Q9.C
  N12: Q4.base, Q6.C
  N13: Q5.base, Q12.C
  N14: R1.CCW, R2.CCW, R3.CCW, R4.CCW, R5.CCW, R6.CCW, J29.pin1
  N15: R1.WIPER, Q6.E
  N16: R2.WIPER, Q12.E, Q14.E
  N17: R3.WIPER, Q11.C, Q13.E
  N18: R4.WIPER, Q11.E
  N19: R5.WIPER, Q7.E
  N20: R6.WIPER, Q7.C, Q9.E, Q10.E
  N21: Q6.B, R7.Pin_1
  N22: R7.Pin_0, J28.pin1
  N23: Q7.B, R11.Pin_1
  N24: J29.pin4, R11.Pin_0, R12.Pin_0
  N25: J29.pin5, R14.Pin_1, R15.Pin_1
  N26: J29.pin6, R13.Pin_1
  N27: R8.Pin_0, Q10.B
  N28: R8.Pin_1, J28.pin2
  N29: Q9.B, R10.Pin_0
  N30: R10.Pin_1, J28.pin3
  N31: Q11.B, R12.Pin_1
  N32: Q12.B, R14.Pin_0
  N33: R13.Pin_0, Q13.B
  N34: Q14.B, R15.Pin_0
  N35: J33_2.pin1, J34.pin2, J35.pin2
  N36: J33_2.pin2, J34.pin1, J35.pin3
  N37: J33_2.pin3, J35.pin1
  N38: J33_2.pin4, J34.pin3

notes:
  A2;A1;A0 SCK;MISO;MOSI;10;9
  8;7;6;Gnd;3,3V,5V
  Konektory:
  Migacz L
  Migacz P
  Konektory: Przód postojówka
  Konektory:Tylne światło, Stop
  Potencjometry:
  Przód Postojówka
  Migacz noc
  Migacz dzień
  Tylne światło dzień
  Tylne światło noc
  Stop
  speed,rpm,5V,Gnd
  speed,gnd,5V
  5V,Gnd,rpm
