# Fritzing sketch Mikrokontroler PCB podst (saved by Fritzing 0.9.3b)
circuit board: 2.36478cm x 2.96523cm
circuit board: 15.6144cm x 6.13307cm
breadboards: 1

parts:
  U1 = atmega328 [package=dip]
  C1 = Ceramic Capacitor [capacitance=100nF package="200 mil [THT, multilayer]"]
  XTAL1 = Crystal [frequency="16 Mhz" package=THT]
  C2 = Ceramic Capacitor [capacitance=22pF package="100 mil [THT, multilayer]"]
  C3 = Ceramic Capacitor [capacitance=22pF package="100 mil [THT, multilayer]"]
  C4 = Ceramic Capacitor [capacitance=100nF package="100 mil [THT, multilayer]"]
  R1 = Resistor [tolerance=±5% resistance=10k package=THT]
  S1 = Pushbutton [package="[THT]"]
  C5 = Ceramic Capacitor [capacitance=100nF package="100 mil [THT, multilayer]"]
  C7 = Ceramic Capacitor [capacitance=100nF package="100 mil [THT, multilayer]"]
  L1 = Inductor [package="400 mil [THT]"]
  GY1 = MPU-6050 Board GY-521 [form="♀ (female)" package=THT]
  C8 = Electrolytic Capacitor [capacitance=1µF package="100 mil [THT, electrolytic]"]
  C9 = Ceramic Capacitor [capacitance=100nF package="100 mil [THT, multilayer]"]
  J1 = male pin header, 4 pins [form="♂ (male)"]
  J4 = male pin header, 5 pins [form="♂ (male)" part_number="na RFID"]
  F1 = Resettable Fuse PTC [package=ptc]
  J5 = male pin header, 2 pins [form="♂ (male)"]
  L2 = Inductor [package="400 mil [THT]"]
  C10 = Electrolytic Capacitor [capacitance=1µF package="100 mil [THT, electrolytic]"]
  C12 = Electrolytic Capacitor [capacitance=1µF package="100 mil [THT, electrolytic]"]
  C13 = Ceramic Capacitor [capacitance=100nF package="100 mil [THT, multilayer]"]
  C14 = Ceramic Capacitor [capacitance=100nF package="100 mil [THT, multilayer]"]
  J6 = male pin header, 3 pins [form="♂ (male)"]
  J2 = male pin header, 7 pins [form="♂ (male)"]
  J3 = male pin header, 5 pins [form="♂ (male)"]
  R3 = Resistor [tolerance=±5% resistance=100k package=THT]
  R4 = Resistor [tolerance=±5% resistance=100k package=THT]
  R5 = Resistor [tolerance=±5% resistance=100k package=THT]
  D2 = Rectifier Diode [part_number=1N4001 package="300 mil [THT]"]
  IC3 = Voltage Regulator LM1117 [package=sot223]
  IC4 = Voltage Regulator LM1117 [package=sot223]

nets:
  N1: U1.RESET, U1.VCC, C1.0, C4.0, R1.Pin_0, R1.Pin_1, S1.Pin_3, S1.Pin_4, L1.pin_0, GY1.pin1, C8.+, C9.0, F1.1, J6.pin1, J2.pin6, J2.pin7
  N2: U1.D0_(RX), J2.pin5
  N3: U1.D1_(TX), J2.pin4
  N4: U1.D2, J2.pin3
  N5: U1.D3_(PWM), J2.pin2
  N6: U1.D4, J2.pin1
  N7: U1.GND, C1.1, C2.1, C3.1, C4.1, S1.Pin_1, S1.Pin_2, C5.0, C7.0, GY1.pin2, C8.-, C9.1, J5.pin1, C10.-, C12.-, C13.1, C14.0, J6.pin2, R4.Pin_0
  N8: U1.XLAT1, XTAL1.pin_1, C2.0
  N9: U1.XLAT2, XTAL1.pin_0, C3.0
  N10: U1.D5_(PWM), J1.pin4
  N11: U1.D6_(PWM), J1.pin3
  N12: U1.D7, J1.pin2
  N13: U1.D8, J1.pin1
  N14: U1.D9_(PWM), J4.pin1
  N15: U1.D10_(PWM), J4.pin2
  N16: U1.D11_(PWM), J4.pin3
  N17: U1.D12, J4.pin4
  N18: U1.D13, J4.pin5
  N19: U1.AVCC, C7.1, L1.pin_1
  N20: U1.AREF, C5.1
  N21: U1.A0, J3.pin1
  N22: U1.A1, J3.pin2
  N23: U1.A2, J3.pin3
  N24: U1.A3, R3.Pin_1, R4.Pin_1
  N25: U1.A4, GY1.pin4, J3.pin4
  N26: U1.A5, GY1.pin3, J3.pin5
  N27: F1.2, C10.+, C14.1
  N28: J5.pin2, L2.pin_1, C12.+
  N29: L2.pin_0, C13.0, D2.anode, IC4.IN
  N30: R3.Pin_0, R5.Pin_0
  N31: D2.cathode, IC3.IN
  N32: IC3.ADJ, IC4.ADJ

notes:
  3,3V
  GND
  5V
  RST;5V;RX;TX;2;3;4 5;6;7;8
  SCL;SDA;A3;A2;A1;A0 SCK;MISO;MOSI;10;9
  Vin
  Gnd

custom parts:
  MPU-6050 Board GY-521: Acelerometro y Giroscopio MPU-6050 Board GY-521
