# Fritzing sketch Mikrokontroler PCB prawa v3 (saved by Fritzing 0.9.3b)
circuit board: 10.0702cm x 17.6965cm
breadboards: 1

parts:
  Pad1 = Pad [width=7.9000000000000004 height=9.0311111111111106 connect=center]  # not connected
  Q1 = Basic FET P-Channel [package="TO220 [THT]"]
  Fuse1 = Fuse with Handler [part_number=Htc-15m]
  IC1 = DIP - 8 pins [part_number=LM741 package="DIP (Dual Inline) [THT]"]
  D1 = Zener Diode [part_number=1N4732A breakdown_voltage=8.2 package="300 mil [THT]"]
  R2 = TRIMPOT [package=trimpot_pth_s3_lock]
  R1 = Resistor [tolerance=±10% resistance=4.7k package=THT]
  J1 = female pin header, 2 pins [form="♀ (female)"]
  D2 = Zener Diode [part_number=1N4732A breakdown_voltage=8.2 package="300 mil [THT]"]
  R3 = Resistor [tolerance=±5% resistance=10k package=THT]
  D3 = Rectifier Diode [part_number=1N4001 package="300 mil [THT]"]
  R4 = TRIMPOT [package=3386u]
  C3 = Electrolytic Capacitor [capacitance=1µF package="100 mil [THT, electrolytic]"]
  OMRON1 = OMRON PCB Power Relay – G5LE [part_number="G5LE-1\n" package=THT]
  Q3 = NPN-Transistor [package="TO92 [THT]"]
  R5 = Resistor [tolerance=±5% resistance=220 package=THT]
  D4 = Rectifier Diode [part_number=1N4001 package="300 mil [THT]"]
  D5 = Diode [package=diode-1n4001]
  D6 = Diode [package=diode-1n4001]
  D7 = Diode [package=diode-1n4001]
  D8 = Diode [package=diode-1n4001]
  Fuse2 = Fuse with Handler [part_number=Htc-15m]
  C4 = Electrolytic Capacitor [capacitance=1µF package="300 mil [THT, electrolytic]"]
  C5 = Electrolytic Capacitor [capacitance=1µF package="200 mil [THT, electrolytic]"]
  J2 = female pin header, 3 pins [form="♀ (female)"]
  OMRON2 = OMRON PCB Power Relay – G5LE [part_number="G5LE-1\n" package=THT]
  Fuse3 = Fuse with Handler [part_number=Htc-15m]
  OMRON3 = OMRON PCB Power Relay – G5LE [part_number="G5LE-1\n" package=THT]
  D9 = Rectifier Diode [part_number=1N4001 package="300 mil [THT]"]
  D10 = Rectifier Diode [part_number=1N4001 package="300 mil [THT]"]
  Q5 = NPN-Transistor [package="TO92 [THT]"]
  Q4 = NPN-Transistor [package="TO92 [THT]"]
  R6 = Resistor [tolerance=±5% resistance=220 package=THT]
  R7 = Resistor [tolerance=±5% resistance=220 package=THT]
  J3 = female pin header, 3 pins [form="♀ (female)"]
  Q2 = NPN-Transistor [package="TO92 [THT]"]

nets:
  N1: Q1.gate, IC1.pin6
  N2: Q1.drain, R4.CCW, Fuse2.Connector2
  N3: Q1.source, Fuse1.Connector2, R3.Pin_0, D3.anode, Q2.C
  N4: Fuse1.Connector1, D5.C, D6.C, C4.+, Fuse3.Connector2
  N5: IC1.pin2, D2.cathode, R3.Pin_1
  N6: IC1.pin3, R4.WIPER
  N7: IC1.pin4, R2.CW, R1.Pin_1, J1.pin1, D2.anode, R4.CW, C3.-, OMRON1.A, OMRON1.B, Q3.E, D7.A, D8.A, C4.-, C5.-, J2.pin2, Q5.E, Q4.E
  N8: IC1.pin7, D3.cathode, C3.+
  N9: D1.cathode, R2.CCW
  N10: D1.anode, R1.Pin_0
  N11: R2.WIPER, Q2.B
  N12: J1.pin2, Q2.E
  N13: OMRON1.COIL1, Q3.B, D4.anode
  N14: OMRON1.COIL2, D4.cathode
  N15: Q3.C, R5.Pin_0
  N16: R5.Pin_1, J3.pin1
  N17: D5.A, D8.C
  N18: D6.A, D7.C
  N19: C5.+, J2.pin3
  N20: J2.pin1, OMRON2.COIL2, OMRON3.COIL1, D9.cathode, D10.cathode
  N21: OMRON2.COIL1, D9.anode, Q4.C
  N22: OMRON2.B, Fuse3.Connector1, OMRON3.B
  N23: OMRON3.COIL2, D10.anode, Q5.C
  N24: Q5.B, R6.Pin_0
  N25: Q4.B, R7.Pin_1
  N26: R6.Pin_1, J3.pin3
  N27: R7.Pin_0, J3.pin2

notes:
  wyjscie na NC stacyjki
  wyjscie na cewke butelkowa
  wejscie z magneta
  Gnd z ramy
  wyjscie na NC stacyjki
  <-- jumper ucc
  wejscie zasilania na NO stacyjki
  wyjscie zasilania na LED
  jumper vcc
  puntk połączeń końców cewek
  GND
  Vcc wentylatora
  Początek 1 cewki
  Początek 2 cewki
  Bezpieczniki
  Na przednie światło

custom parts:
  DIP - 8 pins: A DIP stand-in part for whatever IC you want. With 8 pins on a 300 mil dual inline package (DIP) footprint.
