# Fritzing sketch ELBA 6V (pcb) (saved by Fritzing 0.9.3b)
circuit board: 7.4316cm x 4.99631cm
breadboards: 1

parts:
  D1 = Rectifier Diode [part_number=1N4001 package="300 mil [THT]"]
  R1 = Resistor [tolerance=±5% resistance=220 package=THT]
  R2 = Trimmer Potentiometer [maximum_resistance=10kΩ package=THT]
  Q1 = Basic FET P-Channel [package="TO220 [THT]"]
  R3 = Resistor [tolerance=±5% resistance=220 package=THT]
  LM1 = LM393 [chip_label=?]
  R4 = Resistor [tolerance=±5% resistance=220 package=THT]
  C1 = Electrolytic Capacitor [capacitance=1µF package="100 mil [THT, electrolytic]"]
  D2 = Rectifier Diode [part_number=1N4001 package="300 mil [THT]"]
  Q2 = NPN-Transistor [package="TO92 [THT]"]
  R5 = Resistor [tolerance=±5% resistance=220 package=THT]
  D3 = Zener Diode [part_number=1N4732A breakdown_voltage=3.6V package="300 mil [THT]"]
  R6 = Resistor [tolerance=±5% resistance=220 package=THT]
  R7 = Resistor [tolerance=±5% resistance=220 package=THT]
  R8 = Resistor [tolerance=±5% resistance=220 package=THT]
  D4 = Rectifier Diode [part_number=1N4001 package="300 mil [THT]"]

nets:
  N1: D1.cathode, R1.Pin_0, R8.Pin_0
  N2: D1.anode, Q1.source
  N3: R1.Pin_1, R2.leg1, D3.cathode
  N4: R2.wiper, LM1.In_1_+
  N5: R2.leg2, LM1.Output_2, D3.anode, R6.Pin_1, D4.anode
  N6: Q1.gate, Q2.E, R5.Pin_0
  N7: Q1.drain, R3.Pin_1, LM1.VCC, D2.anode, R5.Pin_1, R7.Pin_0
  N8: R3.Pin_0, LM1.Output_1, R4.Pin_1
  N9: LM1.In_1_-, R6.Pin_0, R7.Pin_1
  N10: R4.Pin_0, C1.-
  N11: C1.+, D2.cathode, Q2.B
  N12: Q2.C, R8.Pin_1
