# Fritzing sketch ELBA 6V (schemat) (saved by Fritzing 0.9.3b)
breadboards: 1

parts:
  U1 = LM393 [part_number=LM393 package=so08]
  D1 = Rectifier Diode [part_number=1N4001 package="Melf DO-213 AB [SMD]"]
  R1 = Resistor [tolerance=±5% resistance=4.7k package=THT]
  D2 = Zener Diode [part_number=1N4732A breakdown_voltage=8.2V package="300 mil [THT]"]
  D3 = Rectifier Diode [part_number=1N4001 package="300 mil [THT]"]
  R3 = Resistor [tolerance=±5% resistance=2.2k package=THT]
  R4 = Resistor [tolerance=±5% resistance=2.2k package=THT]
  R5 = Resistor [tolerance=±5% resistance=620 package=THT]
  R6 = Resistor [tolerance=±5% resistance=270 package=THT]
  D4 = Rectifier Diode [part_number=thyristor package="300 mil [THT]"]
  C1 = Electrolytic Capacitor [capacitance=47µF package="100 mil [THT, electrolytic]"]
  D5 = Rectifier Diode [part_number=1N4001 package="300 mil [THT]"]
  R7 = Resistor [tolerance=±5% resistance=10k package=THT]
  Q1 = NPN-Transistor [package="TO92 [THT]"]
  R8 = Resistor [tolerance=±5% resistance=270 package=THT]
  R9 = Trimmer Potentiometer [maximum_resistance=10kΩ package=THT]

nets:
  N1: U1.G1_OUT, R5.Pin_0, R6.Pin_0
  N2: U1.G1_-IN, R3.Pin_0, R4.Pin_0
  N3: U1.G1_+IN, R9.wiper
  N4: U1.G1_V-, D2.anode, D3.anode, R3.Pin_1, R9.leg1
  Out: U1.G1_V+, R4.Pin_1, R5.Pin_1, D4.cathode, D5.anode, R7.Pin_1
  N5: D1.cathode, R1.Pin_0, R8.Pin_0
  9V: D1.anode, D4.anode
  N6: R1.Pin_1, D2.cathode, R9.leg2
  GND: D3.cathode
  N7: R6.Pin_1, C1.-
  N8: D4.gate, R7.Pin_0, Q1.E
  N9: C1.+, D5.cathode, Q1.B
  N10: Q1.C, R8.Pin_1

notes:
  2.4 V

custom parts:
  Rectifier Diode: A standard rectifier diode
