# Fritzing sketch Mikrokontroler PCB góra.old (saved by Fritzing 0.9.3b)
circuit board: 15.6144cm x 6.13307cm
breadboards: 1

parts:
  J3 = female pin header, 4 pins [form="♀ (female)"]
  J6 = female pin header, 2 pins [form="♀ (female)"]
  J1 = female pin header, 4 pins [form="♀ (female)"]
  J7 = male pin header, 2 pins [form="♂ (male)"]
  Part1 = Bluetooth HC-05 Macho
  R1 = TRIMPOT [package=trimpot_pth_s3_lock]
  R2 = TRIMPOT [package=trimpot_pth_s3_lock]
  R4 = TRIMPOT [package=trimpot_pth_s3_lock]
  R5 = TRIMPOT [package=trimpot_pth_s3_lock]
  R6 = TRIMPOT [package=trimpot_pth_s3_lock]
  Q1 = NPN-Transistor [package="TO92 [THT]"]
  Q2 = npn-Powertransistor [package="TO220 [THT]"]
  Q3 = npn-Powertransistor [package="TO220 [THT]"]
  Q4 = npn-Powertransistor [package="TO220 [THT]"]
  Q5 = npn-Powertransistor [package="TO220 [THT]"]
  R7 = Resistor [tolerance=±5% resistance=220 package=THT]
  R8 = Resistor [tolerance=±5% resistance=220 package=THT]
  R9 = Resistor [tolerance=±5% resistance=220 package=THT]
  R10 = Resistor [tolerance=±5% resistance=220 package=THT]
  Q7 = NPN-Transistor [package="TO92 [THT]"]
  R11 = Resistor [tolerance=±5% resistance=220 package=THT]
  Q8 = NPN-Transistor [package="TO92 [THT]"]
  R12 = Resistor [tolerance=±5% resistance=220 package=THT]
  R13 = Resistor [tolerance=±5% resistance=220 package=THT]
  Q9 = NPN-Transistor [package="TO92 [THT]"]
  Q10 = NPN-Transistor [package="TO92 [THT]"]
  Q11 = NPN-Transistor [package="TO92 [THT]"]
  R14 = Resistor [tolerance=±5% resistance=220 package=THT]
  R15 = Resistor [tolerance=±5% resistance=220 package=THT]
  R16 = Resistor [tolerance=±5% resistance=220 package=THT]
  R17 = Resistor [tolerance=±5% resistance=220 package=THT]
  R18 = Resistor [tolerance=±5% resistance=220 package=THT]
  J4 = male pin header, 5 pins [form="♂ (male)"]
  J2 = female pin header, 4 pins [form="♀ (female)"]
  L1 = Inductor [package="400 mil [THT]"]
  C1 = Electrolytic Capacitor [capacitance=1µF package="100 mil [THT, electrolytic]"]
  C2 = Ceramic Capacitor [capacitance=100nF package="100 mil [THT, multilayer]"]
  J9 = female pin header, 6 pins [form="♀ (female)"]
  J8 = male pin header, 3 pins [form="♂ (male)"]

nets:
  N1: J3.pin1, J9.pin1
  N2: J3.pin2, R13.Pin_0
  N3: J3.pin3, R11.Pin_0
  N4: J3.pin4, R7.Pin_0
  N5: J6.pin1, Part1.GND, R1.CW, R2.CCW, R4.CCW, R5.CCW, R6.CCW, R18.Pin_0, C1.-, C2.1
  N6: J6.pin2, L1.pin_0
  N7: J1.pin1, R17.Pin_0
  N8: J1.pin2, Part1.RXD
  N9: J1.pin3, R12.Pin_0
  N10: J1.pin4, R14.Pin_1, R15.Pin_1
  N11: J7.pin1, J7.pin2, J2.pin1
  N12: Part1.TXD, R17.Pin_1, R18.Pin_1
  N13: Part1.VCC, R2.CW, R4.CW, R5.CW, L1.pin_1, C1.+, C2.0
  N14: R1.CCW, R6.CW, J2.pin2, J8.pin3
  N15: R1.WIPER, Q1.E
  N16: R2.WIPER, Q10.E, Q11.E
  N17: R4.WIPER, Q9.E
  N18: R5.WIPER, Q8.E
  N19: R6.WIPER, Q1.C, Q7.E
  N20: Q1.B, R7.Pin_1
  N21: Q2.base, R8.Pin_0
  N22: Q2.collector, Q3.collector, Q4.collector, Q5.collector
  N23: Q3.base, R10.Pin_0
  N24: Q4.base, R9.Pin_0
  N25: Q5.base, R16.Pin_0
  N26: R8.Pin_1, Q7.C
  N27: R9.Pin_1, Q8.C
  N28: R10.Pin_1, Q9.C, Q11.C
  N29: Q7.B, R11.Pin_1
  N30: Q8.B, R13.Pin_1
  N31: R12.Pin_1, Q9.B
  N32: Q10.B, R14.Pin_0
  N33: Q10.C, R16.Pin_1
  N34: Q11.B, R15.Pin_0
  N35: J4.pin1, J9.pin2
  N36: J4.pin2, J9.pin3
  N37: J4.pin3, J9.pin4
  N38: J4.pin4, J9.pin5
  N39: J4.pin5, J9.pin6
  N40: J2.pin3, J8.pin2
  N41: J2.pin4, J8.pin1

notes:
  Potencjometry: Migacze noc, Migacze dzień, Tylnie światło, Stop, Przód postojówka
  Konektory: Migacz, Przód postojówka, Tylne światło, Stop
