# Fritzing sketch Mikrokontroler PCB prawa v.2 (saved by Fritzing 0.9.3b)
circuit board: 6.93405cm x 13.2849cm
breadboards: 1

parts:
  D1 = Rectifier Diode [part_number=1N4001 package="300 mil [THT]"]
  R1 = Resistor [tolerance=±5% resistance=220 package=THT]
  Q1 = Basic FET P-Channel [package="TO220 [THT]"]
  R3 = Resistor [tolerance=±5% resistance=220 package=THT]
  LM1 = LM393 [chip_label=?]
  R4 = Resistor [tolerance=±5% resistance=220 package=THT]
  C1 = Electrolytic Capacitor [capacitance=1µF package="100 mil [THT, electrolytic]"]
  D2 = Rectifier Diode [part_number=1N4001 package="300 mil [THT]"]
  Q2 = NPN-Transistor [package="TO92 [THT]"]
  R5 = Resistor [tolerance=±5% resistance=10k package=THT]
  D3 = Zener Diode [part_number=1N4732A breakdown_voltage=8.2V package="300 mil [THT]"]
  R6 = Resistor [tolerance=±5% resistance=2.2k package=THT]
  R7 = Resistor [tolerance=±5% resistance=2.2k package=THT]
  R8 = Resistor [tolerance=±5% resistance=270 package=THT]
  D7 = Diode [package=diode-1n4001]
  D8 = Diode [package=diode-1n4001]
  D9 = Diode [package=diode-1n4001]
  D10 = Diode [package=diode-1n4001]
  C2 = Electrolytic Capacitor [capacitance=1µF package="300 mil [THT, electrolytic]"]
  C3 = Electrolytic Capacitor [capacitance=1µF package="200 mil [THT, electrolytic]"]
  J1 = female pin header, 2 pins [form="♀ (female)"]
  Fuse4 = Fuse with Handler [part_number=Htc-15m]
  Fuse5 = Fuse with Handler [part_number=Htc-15m]
  K1 = OMRON PCB Power Relay – G5LE [part_number="G5LE-1\n" package=THT]
  D11 = Diode [package=diode-1n4148]
  Q3 = NPN-Transistor [package="TO92 [THT]"]
  R9 = Resistor [tolerance=±5% resistance=220 package=THT]
  K2 = OMRON PCB Power Relay – G5LE [part_number="G5LE-1\n" package=THT]
  Q4 = NPN-Transistor [package="TO92 [THT]"]
  R10 = Resistor [tolerance=±5% resistance=220 package=THT]
  D12 = Diode [package=diode-1n4148]
  K3 = OMRON PCB Power Relay – G5LE [part_number="G5LE-1\n" package=THT]
  R11 = Resistor [tolerance=±5% resistance=220 package=THT]
  Q5 = PNP-Transistor [package="TO92 [THT]"]
  J2 = female pin header, 3 pins [form="♀ (female)"]
  R12 = Resistor [tolerance=±5% resistance=220 part_number=Diode package=THT]
  R13 = TRIMPOT [package=trimpot_pth_s3_lock]
  J3 = female pin header, 2 pins [form="♀ (female)"]
  R14 = Resistor [tolerance=±5% resistance=10k package=THT]

nets:
  N1: D1.cathode, R1.Pin_0, R8.Pin_0
  N2: D1.anode, Q1.source, Fuse4.Connector2, K1.B, K3.B
  N3: R1.Pin_1, D3.cathode, R13.CW
  N4: Q1.gate, Q2.E, R5.Pin_0
  N5: Q1.drain, R3.Pin_1, LM1.VCC, D2.anode, R5.Pin_1, R7.Pin_0, C3.+, Fuse5.Connector1, K1.COIL2, D11.C, K2.COIL1, D12.C, Q5.E, R14.Pin_0
  N6: R3.Pin_0, LM1.Output_1, R4.Pin_1
  N7: LM1.In_1_-, R6.Pin_0, R7.Pin_1
  N8: LM1.In_1_+, R13.WIPER
  N9: LM1.Output_2, D3.anode, R6.Pin_1, D7.A, D10.A, C2.-, C3.-, Q3.E, Q4.E, K3.COIL1, R12.Pin_1, R13.CCW, J3.pin2
  N10: R4.Pin_0, C1.-
  N11: C1.+, D2.cathode, Q2.B
  N12: Q2.C, R8.Pin_1
  N13: D7.C, D8.A, D9.A, D10.C
  N14: D8.C, D9.C, C2.+, Fuse4.Connector1
  N15: J1.pin1, Fuse5.Connector2
  N16: J1.pin2, J3.pin1
  N17: K1.COIL1, D11.A, Q3.C
  N18: Q3.B, R9.Pin_0
  N19: R9.Pin_1, J2.pin1
  N20: K2.COIL2, Q4.C, D12.A
  N21: Q4.B, R10.Pin_0
  N22: R10.Pin_1, J2.pin2
  N23: K3.COIL2, Q5.C, R12.Pin_0
  N24: R11.Pin_0, Q5.B, R14.Pin_1
  N25: R11.Pin_1, J2.pin3

notes:
  aku+
  aku-
  Vcc
  Gnd
  Sw1
  Sw2
  Światło mijania
  Zapłon
  Światło drogowe
