# Fritzing sketch Mikrokontroler PCB prawa (saved by Fritzing 0.9.3b)
circuit board: 9.56994cm x 17.0383cm
breadboards: 1

parts:
  D1 = Rectifier Diode [part_number=1N4001 package="300 mil [THT]"]
  R1 = Resistor [tolerance=±5% resistance=220 package=THT]
  R2 = Trimmer Potentiometer [maximum_resistance=10kΩ package=THT]
  Q1 = Basic FET P-Channel [package="TO220 [THT]"]
  R3 = Resistor [tolerance=±5% resistance=220 package=THT]
  LM1 = LM393 [chip_label=?]
  R4 = Resistor [tolerance=±5% resistance=220 package=THT]
  C1 = Electrolytic Capacitor [capacitance=1µF package="100 mil [THT, electrolytic]"]
  D2 = Rectifier Diode [part_number=1N4001 package="300 mil [THT]"]
  Q2 = NPN-Transistor [package="TO92 [THT]"]
  R5 = Resistor [tolerance=±5% resistance=220 package=THT]
  D3 = Zener Diode [part_number=1N4732A breakdown_voltage=3.6V package="300 mil [THT]"]
  R6 = Resistor [tolerance=±5% resistance=220 package=THT]
  R7 = Resistor [tolerance=±5% resistance=220 package=THT]
  R8 = Resistor [tolerance=±5% resistance=220 package=THT]
  D4 = Rectifier Diode [part_number=1N4001 package="300 mil [THT]"]
  D7 = Diode [package=diode-1n4001]
  D8 = Diode [package=diode-1n4001]
  D9 = Diode [package=diode-1n4001]
  D10 = Diode [package=diode-1n4001]
  C2 = Electrolytic Capacitor [capacitance=1µF package="300 mil [THT, electrolytic]"]
  C3 = Electrolytic Capacitor [capacitance=1µF package="200 mil [THT, electrolytic]"]
  J1 = female pin header, 2 pins [form="♀ (female)"]
  Fuse4 = Fuse with Handler [part_number=Htc-15m]
  Fuse5 = Fuse with Handler [part_number=Htc-15m]
  K1 = OMRON PCB Power Relay – G5LE [part_number="G5LE-1\n" package=THT]
  D11 = Diode [package=diode-1n4148]
  Q3 = NPN-Transistor [package="TO92 [THT]"]
  R9 = Resistor [tolerance=±5% resistance=220 package=THT]
  K2 = OMRON PCB Power Relay – G5LE [part_number="G5LE-1\n" package=THT]
  Q4 = NPN-Transistor [package="TO92 [THT]"]
  R10 = Resistor [tolerance=±5% resistance=220 package=THT]
  D12 = Diode [package=diode-1n4148]
  J2 = female pin header, 2 pins [form="♀ (female)"]

nets:
  N1: D1.cathode, R1.Pin_0, R8.Pin_0
  N2: D1.anode, Q1.source, Fuse4.Connector2, K1.B
  N3: R1.Pin_1, R2.leg1, D3.cathode
  N4: R2.wiper, LM1.In_1_+
  N5: R2.leg2, LM1.Output_2, D3.anode, R6.Pin_1, D4.anode
  N6: Q1.gate, Q2.E, R5.Pin_0
  N7: Q1.drain, R3.Pin_1, LM1.VCC, D2.anode, R5.Pin_1, R7.Pin_0, C3.+, Fuse5.Connector1, K1.COIL2, D11.C, K2.COIL1, D12.C
  N8: R3.Pin_0, LM1.Output_1, R4.Pin_1
  N9: LM1.In_1_-, R6.Pin_0, R7.Pin_1
  N10: R4.Pin_0, C1.-
  N11: C1.+, D2.cathode, Q2.B
  N12: Q2.C, R8.Pin_1
  N13: D4.cathode, D7.A, D10.A, C2.-, C3.-, J1.pin2, Q3.E, Q4.E
  N14: D7.C, D8.A, D9.A, D10.C
  N15: D8.C, D9.C, C2.+, Fuse4.Connector1
  N16: J1.pin1, Fuse5.Connector2
  N17: K1.COIL1, D11.A, Q3.C
  N18: Q3.B, R9.Pin_0
  N19: R9.Pin_1, J2.pin1
  N20: K2.COIL2, Q4.C, D12.A
  N21: Q4.B, R10.Pin_0
  N22: R10.Pin_1, J2.pin2

notes:
  aku+
  aku-
  Vcc
  Gnd
  Zapłon
  Przód światlo
