# Fritzing sketch Mikrokontroler PCB (saved by Fritzing 0.9.3b)
circuit board: 26.4943cm x 17.2577cm
breadboards: 1

parts:
  U1 = atmega328 [package=dip]
  C1 = Ceramic Capacitor [capacitance=100nF package="200 mil [THT, multilayer]"]
  XTAL1 = Crystal [frequency="16 Mhz" package=THT]
  C2 = Ceramic Capacitor [capacitance=22pF package="100 mil [THT, multilayer]"]
  C3 = Ceramic Capacitor [capacitance=22pF package="100 mil [THT, multilayer]"]
  C4 = Ceramic Capacitor [capacitance=100nF package="100 mil [THT, multilayer]"]
  R1 = Resistor [tolerance=±5% resistance=220 package=THT]
  R2 = Resistor [tolerance=±5% resistance=220 package=THT]
  S1 = Pushbutton [package="[THT]"]
  D1 = Rectifier Diode [part_number=1N4001 package="300 mil [THT]"]
  C5 = Ceramic Capacitor [capacitance=100nF package="100 mil [THT, multilayer]"]
  C7 = Ceramic Capacitor [capacitance=100nF package="100 mil [THT, multilayer]"]
  L1 = Inductor [package="400 mil [THT]"]
  D2 = Zener Diode [part_number=1N4732A breakdown_voltage=4.7V package="300 mil [THT]"]
  Q1 = npn-Powertransistor [package="TO220 [THT]"]
  R3 = Trimmer Potentiometer [maximum_resistance=10kΩ package=THT]
  R4 = Resistor [tolerance=±5% resistance=220 package=THT]
  R5 = Trimmer Potentiometer [maximum_resistance=10kΩ package=THT]
  Q2 = NPN-Transistor [package="TO92 [THT]"]
  R6 = Resistor [tolerance=±5% resistance=220 package=THT]
  Q3 = NPN-Transistor [package="TO92 [THT]"]
  R7 = Resistor [tolerance=±5% resistance=220 package=THT]
  GY1 = MPU-6050 Board GY-521 [form="♀ (female)" package=THT]
  C8 = Electrolytic Capacitor [capacitance=1µF package="100 mil [THT, electrolytic]"]
  C9 = Ceramic Capacitor [capacitance=100nF package="100 mil [THT, multilayer]"]
  D3 = Zener Diode [part_number=1N4732A breakdown_voltage=4.7V package="300 mil [THT]"]
  Q4 = npn-Powertransistor [package="TO220 [THT]"]
  R9 = Trimmer Potentiometer [maximum_resistance=10kΩ package=THT]
  R10 = Resistor [tolerance=±5% resistance=220 package=THT]
  R11 = Resistor [tolerance=±5% resistance=220 package=THT]
  Q6 = NPN-Transistor [package="TO92 [THT]"]
  R8 = Trimmer Potentiometer [maximum_resistance=10kΩ package=THT]
  D4 = Zener Diode [part_number=1N4732A breakdown_voltage=4.7V package="300 mil [THT]"]
  Q7 = npn-Powertransistor [package="TO220 [THT]"]
  R14 = Trimmer Potentiometer [maximum_resistance=10kΩ package=THT]
  R15 = Resistor [tolerance=±5% resistance=220 package=THT]
  R16 = Resistor [tolerance=±5% resistance=220 package=THT]
  Q9 = NPN-Transistor [package="TO92 [THT]"]
  Q10 = NPN-Transistor [package="TO92 [THT]"]
  R18 = Resistor [tolerance=±5% resistance=220 package=THT]
  R19 = Resistor [tolerance=±5% resistance=220 package=THT]
  Q11 = npn-Powertransistor [package="TO220 [THT]"]
  R20 = Resistor [tolerance=±5% resistance=220 package=THT]
  Q12 = NPN-Transistor [package="TO92 [THT]"]
  C10 = Ceramic Capacitor [capacitance=100nF package="100 mil [THT, multilayer]"]
  C11 = Electrolytic Capacitor [capacitance=1μF package="200 mil [THT, electrolytic]"]
  Q13 = NPN-Transistor [package="TO92 [THT]"]
  D5 = Rectifier Diode [part_number=1N4001 package="300 mil [THT]"]
  R21 = Resistor [tolerance=±5% resistance=220 package=THT]

nets:
  N1: U1.RESET, C4.0, R1.Pin_0, S1.Pin_3, S1.Pin_4, D1.anode
  N2: U1.D4, R21.Pin_0
  N3: U1.VCC, C1.0, R1.Pin_1, D1.cathode, L1.pin_0, R3.leg2, R5.leg2, GY1.pin1, C8.+, C9.0, R9.leg2, R8.leg2, R14.leg2, D5.cathode
  N4: U1.GND, C1.1, C2.1, C3.1, C4.1, R2.Pin_0, C5.0, C7.0, D2.anode, R3.leg1, R5.leg1, GY1.pin2, C8.-, C9.1, D3.anode, R9.leg1, R8.leg1, D4.anode, R14.leg1, C10.0, C11.-, Q13.E
  N5: U1.XLAT1, XTAL1.pin_1, C2.0
  N6: U1.XLAT2, XTAL1.pin_0, C3.0
  N7: U1.D5_(PWM), R7.Pin_1
  N8: U1.D6_(PWM), R16.Pin_0, R19.Pin_0
  N9: U1.D7, R11.Pin_0
  N10: U1.D8, R6.Pin_0
  N11: U1.D9_(PWM), Q12.B
  N12: U1.AVCC, C7.1, L1.pin_1
  N13: U1.AREF, C5.1
  N14: U1.A4, GY1.pin4
  N15: U1.A5, GY1.pin3
  N16: R2.Pin_1, S1.Pin_2
  N17: D2.cathode, Q1.base, Q3.C
  N18: Q1.collector, Q4.collector, Q7.collector, Q11.collector, C10.1, C11.+
  N19: R3.wiper, R4.Pin_1, Q2.C
  N20: R4.Pin_0, Q3.E
  N21: R5.wiper, Q2.E
  N22: Q2.B, R7.Pin_0
  N23: R6.Pin_1, Q3.B
  N24: D3.cathode, Q4.base, Q6.C, Q10.C
  N25: R9.wiper, R10.Pin_1
  N26: R10.Pin_0, Q6.E
  N27: R11.Pin_1, Q6.B
  N28: R8.wiper, R20.Pin_1
  N29: D4.cathode, Q7.base, Q9.C
  N30: R14.wiper, R15.Pin_1, R18.Pin_1
  N31: R15.Pin_0, Q9.E
  N32: R16.Pin_1, Q9.B
  N33: Q10.E, R18.Pin_0
  N34: Q10.B, R19.Pin_1
  N35: Q11.base, Q12.C
  N36: R20.Pin_0, Q12.E
  N37: Q13.B, R21.Pin_1
  N38: Q13.C, D5.anode

notes:
  Potencjometry: Migacze noc, Migacze dzień, Tylnie światło, Stop, Przód postojówka
  Konektory: Migacz, Przód postojówka, Tylne światło, Stop

custom parts:
  MPU-6050 Board GY-521: Acelerometro y Giroscopio MPU-6050 Board GY-521
