# Fritzing sketch Przerywacz MOSFET (saved by Fritzing 0.9.3b)
circuit board: 5.34135cm x 4.62293cm
breadboards: 1

parts:
  IC1 = General purpose bipolar Timer [part_number="NE 555" package=dil-08]
  R1 = TRIMPOT [package=trimpot_pth_s3_lock]
  R2 = TRIMPOT [package=trimpot_pth_s3_lock]
  C1 = Electrolytic Capacitor [capacitance=1µF package="100 mil [THT, electrolytic]"]
  C2 = Ceramic Capacitor [capacitance=100nF package="200 mil [THT, multilayer]"]
  Q1 = Basic FET P-Channel [package="TO220 [THT]"]
  Q2 = Basic FET P-Channel [package="TO220 [THT]"]
  R3 = Resistor [tolerance=±5% resistance=220 package=THT]

nets:
  N1: IC1.GND, C1.-, C2.1
  N2: IC1.TRI, IC1.TRE, R2.CW, C1.+
  N3: IC1.OUT, R3.Pin_1
  N4: IC1._RES, IC1.VCC+, R1.CCW, R1.WIPER, Q1.source, Q2.source
  N5: IC1.CON, C2.0
  N6: IC1.DIS, R1.CW, R2.CCW, R2.WIPER
