# Fritzing sketch Przerywacz Relay (saved by Fritzing 0.9.3b)
circuit board: 8.11015cm x 4.25495cm
breadboards: 1

parts:
  IC1 = General purpose bipolar Timer [part_number="NE 555" package=dil-08]
  R1 = TRIMPOT [package=trimpot_pth_s3_lock]
  R2 = TRIMPOT [package=trimpot_pth_s3_lock]
  C1 = Electrolytic Capacitor [capacitance=1µF package="100 mil [THT, electrolytic]"]
  C2 = Ceramic Capacitor [capacitance=100nF package="200 mil [THT, multilayer]"]
  Q1 = PNP-Transistor [package="TO92 [THT]"]
  Q2 = PNP-Transistor [package="TO92 [THT]"]
  D1 = Rectifier Diode [part_number=1N4001 package="300 mil [THT]"]
  D2 = Diode [package=diode-1n4001]
  R3 = Resistor [tolerance=±5% resistance=220 package=THT]
  R4 = Resistor [tolerance=±5% resistance=220 package=THT]
  D3 = Diode [package=diode-1n4001]

nets:
  N1: IC1.GND, C1.-, C2.1, Q1.E, Q2.E
  N2: IC1.TRI, IC1.TRE, R2.CW, C1.+
  N3: IC1._RES, IC1.VCC+, R1.CCW, R1.WIPER, D1.cathode, D2.C, D3.C
  N4: IC1.CON, C2.0
  N5: IC1.DIS, R1.CW, R2.CCW, R2.WIPER
  N6: Q1.B, R3.Pin_1
  N7: Q1.C, D3.A
  N8: Q2.B, R4.Pin_1
  N9: Q2.C, D2.A
