# Fritzing sketch Dół (saved by Fritzing 0.9.3b)
breadboards: 1

parts:
  C1 = Electrolytic Capacitor [capacitance=0.1mF package="100 mil [THT, electrolytic]"]
  L1 = Inductor [package="400 mil [THT]"]
  C2 = Ceramic Capacitor [capacitance=100nF package="100 mil [THT, multilayer]"]
  C3 = Electrolytic Capacitor [capacitance=1mF package="100 mil [THT, electrolytic]"]
  IC1 = Voltage Regulator [part_number="LM 1117 5V" package=78xxl]
  IC2 = Voltage Regulator [part_number="LM 1117 3.3V" package=78xxl]
  D1 = Schottky Diode [part_number=1N5817 package="300 mil [THT]"]
  D4 = Rectifier Diode [part_number=1N4001 package="300 mil [THT]"]
  C4 = Electrolytic Capacitor [capacitance=0.1mF package="100 mil [THT, electrolytic]"]
  C5 = Ceramic Capacitor [capacitance=100nF package="100 mil [THT, multilayer]"]
  F1 = Resettable Fuse PTC [package=0603]
  D2 = Schottky Diode [part_number=1N5817 package="300 mil [THT]"]
  D3 = Schottky Diode [part_number=1N5817 package="300 mil [THT]"]
  U1 = atmega328 [package=dip]
  D5 = Rectifier Diode [part_number=Transil package="300 mil [THT]"]
  D6 = Rectifier Diode [part_number=Transil package="300 mil [THT]"]
  XTAL1 = Crystal [frequency="16 Mhz" package=THT]
  C6 = Ceramic Capacitor [capacitance=22nF package="100 mil [THT, multilayer]"]
  C7 = Ceramic Capacitor [capacitance=22nF package="100 mil [THT, multilayer]"]
  C8 = Ceramic Capacitor [capacitance=100nF package="100 mil [THT, multilayer]"]
  C9 = Ceramic Capacitor [capacitance=1nF package="100 mil [THT, multilayer]"]
  C10 = Ceramic Capacitor [capacitance=100nF package="100 mil [THT, multilayer]"]
  R1 = Resistor [tolerance=±5% resistance=10k package=THT]
  D7 = Rectifier Diode [part_number=1N4001 package="300 mil [THT]"]
  S1 = Pushbutton [package="[THT]"]
  R2 = Resistor [tolerance=±5% resistance=100k package=THT]
  R3 = Resistor [tolerance=±5% resistance=100k package=THT]
  R4 = Resistor [tolerance=±5% resistance=100k package=THT]
  L2 = Inductor [package="400 mil [THT]"]
  C11 = Ceramic Capacitor [capacitance=100nF package="100 mil [THT, multilayer]"]
  C12 = Ceramic Capacitor [capacitance=100nF package="100 mil [THT, multilayer]"]
  GY1 = MPU-6050 GY-521 [form="♀ (female)"]
  C13 = Ceramic Capacitor [capacitance=100nF package="100 mil [THT, multilayer]"]
  C14 = Electrolytic Capacitor [capacitance=0.1mF package="100 mil [THT, electrolytic]"]

nets:
  GND: C1.-, D4.cathode
  Zasilanie mikrokontrolera: C1.+, L1.pin_0
  N1: L1.pin_1, C2.1, C3.+, IC1.IN, D1.anode, D3.cathode, R4.Pin_1
  0V: C2.0, C3.-, IC1.GND, IC2.GND, D4.anode, C4.-, C5.0, U1.GND, D5.cathode, D6.cathode, C6.0, C7.0, C8.0, C9.0, C10.1, S1.Pin_3, S1.Pin_4, R3.Pin_1, C11.0, C12.1, GY1.connector1, C13.0, C14.-
  N2: IC1.OUT, C4.+, C5.1, F1.2, D3.anode, D5.anode
  N3: IC2.IN, D1.cathode, D2.cathode
  3.3V: IC2.OUT, D2.anode, D6.anode
  5V: F1.1, U1.VCC, C8.1, C9.1, R1.Pin_1, D7.cathode, L2.pin_1, GY1.connector0, C13.1, C14.+
  N4: U1.RESET, C10.0, R1.Pin_0, D7.anode, S1.Pin_1, S1.Pin_2
  RX: U1.D0_(RX)
  TX: U1.D1_(TX)
  2: U1.D2
  3: U1.D3_(PWM)
  4: U1.D4
  N5: U1.XLAT1, XTAL1.pin_1, C6.1
  N6: U1.XLAT2, XTAL1.pin_0, C7.1
  5: U1.D5_(PWM)
  6: U1.D6_(PWM)
  7: U1.D7
  8: U1.D8
  9: U1.D9_(PWM)
  10: U1.D10_(PWM)
  11: U1.D11_(PWM)
  12: U1.D12
  13: U1.D13
  N7: U1.AVCC, L2.pin_0, C11.1
  N8: U1.AREF, C12.0
  N9: U1.A3, R2.Pin_0, R4.Pin_0
  SDA: U1.A4, GY1.connector3
  SCL: U1.A5, GY1.connector2
  N10: R2.Pin_1, R3.Pin_0

notes:
  MPU
  6050
