# Fritzing sketch Góra (saved by Fritzing 0.9.3b)
breadboards: 1

parts:
  R1 = TRIMPOT [part_number=Postojówka package=trimpot-3mm]
  R2 = TRIMPOT [part_number=Stop package=trimpot-3mm]
  R3 = TRIMPOT [part_number="Tylne światło noc" package=trimpot-3mm]
  R4 = TRIMPOT [part_number="Tylne światło dzień" package=trimpot-3mm]
  R5 = TRIMPOT [part_number="Migacz dzień" package=trimpot-3mm]
  R6 = TRIMPOT [part_number="Migacz noc" package=trimpot-3mm]
  Q1 = NPN-Transistor [package="SOT-23 [SMD]"]
  Q2 = NPN-Transistor [package="SOT-23 [SMD]"]
  Q3 = NPN-Transistor [package="SOT-23 [SMD]"]
  Q4 = NPN-Transistor [package="SOT-23 [SMD]"]
  Q5 = NPN-Transistor [package="SOT-23 [SMD]"]
  Q6 = NPN-Transistor [package="SOT-23 [SMD]"]
  Q7 = NPN-Transistor [package="SOT-23 [SMD]"]
  Q8 = NPN-Transistor [package="SOT-23 [SMD]"]
  R7 = Resistor [tolerance=±5% resistance=1k package=THT]
  R8 = Resistor [tolerance=±5% resistance=1k package=THT]
  R9 = Resistor [tolerance=±5% resistance=1k package=THT]
  R10 = Resistor [tolerance=±5% resistance=1k package=THT]
  R11 = Resistor [tolerance=±5% resistance=1k package=THT]
  R12 = Resistor [tolerance=±5% resistance=1k package=THT]
  R13 = Resistor [tolerance=±5% resistance=1k package=THT]
  R14 = Resistor [tolerance=±5% resistance=1k package=THT]
  Q9 = NPN-Transistor [package="SOT-23 [SMD]"]
  Q10 = NPN-Transistor [package="SOT-23 [SMD]"]
  Q11 = NPN-Transistor [package="SOT-23 [SMD]"]
  Q12 = NPN-Transistor [package="SOT-23 [SMD]"]
  Q13 = NPN-Transistor [package="SOT-23 [SMD]"]

nets:
  0V: R1.CCW, R2.CCW, R3.CCW, R4.CCW, R5.CCW, R6.CCW
  N1: R1.WIPER, Q1.1
  5V: R1.CW, R2.CW, R3.CW, R4.CW, R5.CW, R6.CW
  N2: R2.WIPER, Q7.1, Q8.1
  N3: R3.WIPER, Q5.2, Q6.1
  N4: R4.WIPER, Q5.1
  N5: R5.WIPER, Q2.1
  N6: R6.WIPER, Q2.2, Q3.1, Q4.1
  N7: Q1.2, Q13.0
  N8: Q1.0, R9.Pin_0
  N9: Q2.0, R8.Pin_0
  N10: Q3.2, Q12.0
  N11: Q3.0, R10.Pin_0
  N12: Q4.2, Q11.0
  N13: Q4.0, R11.Pin_0
  N14: Q5.0, R7.Pin_0
  N15: Q6.2, Q10.0
  N16: Q6.0, R12.Pin_0
  N17: Q7.2, Q8.2, Q9.0
  N18: Q7.0, R13.Pin_0
  N19: Q8.0, R14.Pin_0
  6: R7.Pin_1, R8.Pin_1
  A0: R9.Pin_1
  A1: R10.Pin_1
  A2: R11.Pin_1
  8: R12.Pin_1
  7: R13.Pin_1, R14.Pin_1
  Stop/Tylne światło: Q9.2, Q10.2
  Zasilanie LED: Q9.1, Q10.1, Q11.1, Q12.1, Q13.1
  Prawy migacz: Q11.2
  Lewy migacz: Q12.2
  Światło postojowe: Q13.2
