# Fritzing sketch Prawa (saved by Fritzing 0.9.3b)
breadboards: 1

parts:
  D1 = Schottky Diode [part_number=1N5817 package="300 mil [THT]"]
  D2 = Schottky Diode [part_number=1N5817 package="300 mil [THT]"]
  D3 = Schottky Diode [part_number=1N5817 package="300 mil [THT]"]
  D4 = Schottky Diode [part_number=1N5817 package="300 mil [THT]"]
  C1 = Electrolytic Capacitor [capacitance=1mF package="100 mil [THT, electrolytic]"]
  Fuse1 = Fuse with Handler [part_number=Htc-15m]
  Fuse2 = Fuse with Handler [part_number=Htc-15m]
  U2 = RELAY [package=relay-g5q]
  U3 = RELAY [package=relay-g5q]
  Q1 = NPN-Transistor [package="TO92 [THT]"]
  Q2 = NPN-Transistor [package="TO92 [THT]"]
  R1 = Resistor [tolerance=±5% resistance=1k package=THT]
  R2 = Resistor [tolerance=±5% resistance=1k package=THT]
  D5 = Rectifier Diode [part_number=1N4001 package="300 mil [THT]"]
  D6 = Rectifier Diode [part_number=1N4001 package="300 mil [THT]"]
  IC1 = DIP___8_pins [part_number=LM741]
  Q3 = Basic FET P-Channel [package="TO220 [THT]"]
  D7 = Zener Diode [part_number=1N4732A breakdown_voltage=3.6V package="300 mil [THT]"]
  R3 = Resistor [tolerance=±5% resistance=10k package=THT]
  R4 = Trimmer Potentiometer [maximum_resistance=10kΩ package=THT]
  R5 = Trimmer Potentiometer [maximum_resistance=10kΩ package=THT]
  Q4 = NPN-Transistor [package="TO92 [THT]"]
  Fuse3 = Fuse with Handler [part_number=Htc-15m]
  L1 = Inductor [package="400 mil [THT]"]
  D8 = Rectifier Diode [part_number="Transil 9,6 V" package="300 mil [THT]"]
  C2 = Electrolytic Capacitor [capacitance=1mF package="100 mil [THT, electrolytic]"]
  C3 = Capacitor Polarized [part_number=10mF package=nippon_f80]
  U4 = RELAY [package=relay-g5q]
  Q5 = TRANSISTOR_NPN [package=to-92-ammo]
  R6 = Resistor [tolerance=±5% resistance=1k package=THT]
  D9 = Rectifier Diode [part_number=1N4001 package="300 mil [THT]"]
  D10 = Rectifier Diode [part_number=1N4001 package="300 mil [THT]"]
  C4 = Ceramic Capacitor [capacitance=100nF package="100 mil [THT, multilayer]"]

nets:
  N1: D1.cathode, D3.cathode, C1.+, Fuse1.Connector1, Fuse2.Connector1
  U1: D1.anode, D4.cathode
  V1: D2.cathode, D3.anode
  - Fan/GND: D2.anode, D4.anode, C1.-, Q1.E, Q2.E, IC1.connector3, D7.anode, R4.leg1, R5.leg1, D8.cathode, C2.-, C3.-, U4.NO, Q5.E, C4.1
  N2: Fuse1.Connector2, U2.MAIN, U3.MAIN
  N3: Fuse2.Connector2, Q3.source, R3.Pin_0, R4.leg2, R5.leg2, Q4.C, D10.anode
  N4: U2.COIL2, Q2.C, D5.anode
  Światło mijania: U2.NO
  5V: U2.COIL1, U3.COIL2, D5.cathode, D6.cathode, U4.COIL1, D9.cathode
  Światło drogowe: U3.NO
  N5: U3.COIL1, Q1.C, D6.anode
  N6: Q1.B, R2.Pin_1
  N7: Q2.B, R1.Pin_1
  Uc_Świało mijania: R1.Pin_0
  Uc_Świało drogowe: R2.Pin_0
  N8: IC1.connector1, D7.cathode, R3.Pin_1
  N9: IC1.connector2, R4.wiper
  N10: IC1.connector5, Q3.gate
  N11: IC1.connector6, D10.cathode, C4.0
  N12: Q3.drain, L1.pin_1, D8.anode
  N13: R5.wiper, Q4.B
  + Fan: Q4.E
  7.24V/Zasilanie LED/Zasilanie mikrokontrolera: Fuse3.Connector1, L1.pin_0, C2.+, C3.+
  Ucc: Fuse3.Connector2
  N14: U4.COIL2, Q5.C, D9.anode
  Zapłon/Zapłon 1/Zapłon 2: U4.MAIN
  N15: Q5.B, R6.Pin_1
  Uc_Gaszenie: R6.Pin_0
