# Fritzing sketch Schemat instalacji ogólny (saved by Fritzing 0.9.3b)
breadboards: 1

parts:
  Postojówka = gg
  Migacz_lewy = gg
  Migacz_lewy1 = gg
  Blinda = Square Pushbutton
  Klakson = Square Pushbutton
  Migacze = SWITCH_SPDT [package=kps-1290]
  Światła = SWITCH_SPDT [package=kps-1290]
  Żarówka1 = ggg [part_number="Przednia lampa"]
  L1 = Inductor [package="400 mil [THT]"]
  L2 = Inductor [package="400 mil [THT]"]
  L3 = Inductor [package="400 mil [THT]"]
  Żarówka2 = ggg [part_number="Przednia lampa"]
  Migacz_lewy_tyl = gg
  Migacz_prawy_tyl = gg
  Tr1 = prefix0000 [part_number="Cewka zapłonowa"]
  J1 = double row male pin header, 4 pins [form="♂ (male)"]
  J1_2 = double row rounded female pin header, 4 pins [form="♀ (female rounded)" part_number=Kostka]
  S1 = SWITCH-SPST-2 [part_number="Stacyjka NC i NO" package=r_sw_th]
  S2 = SWITCH-SPST-2 [package=r_sw_th]
  S3 = Pushbutton [part_number="Czujnik hamulca tyl" package="[THT]"]
  S4 = Pushbutton [part_number="Czujnik hamulca przód" package="[THT]"]

nets:
  GND: Postojówka.connector1, Migacz_lewy.connector2, Migacz_lewy1.connector2, Klakson.leg1, Żarówka1.connector1, L3.pin_0, Migacz_lewy_tyl.connector2, Migacz_prawy_tyl.connector1, Tr1.connector0, J1.pin4
  Światło postojowe: Postojówka.connector2
  Lewy migacz: Migacz_lewy.connector1, Migacz_lewy_tyl.connector1
  Prawy migacz: Migacz_lewy1.connector1, Migacz_prawy_tyl.connector2
  Manetka blinda: Blinda.leg0
  Masa manetki: Blinda.leg1, Migacze.P, Światła.P, S4.Pin_1, S4.Pin_2
  Klakson -: Klakson.leg0
  Manetka lewy migacz: Migacze.O
  Manetka prawy migacz: Migacze.S
  Manetka swiatlo drogowe: Światła.O
  Manetka swiatlo kierunkowe: Światła.S
  Światło kierunkowe: Żarówka1.connector2
  Światło drogowe: Żarówka1.connector3
  U1: L1.pin_0
  U2: L1.pin_1
  V2: L2.pin_0
  V1: L2.pin_1
  Zapłon: L3.pin_1
  Gnd: Żarówka2.connector1
  Stop: Żarówka2.connector2
  Tylne światło: Żarówka2.connector3
  Zapłon 1/Zapłon 2: Tr1.connector2, J1.pin3
  Ucc: J1.pin1
  Akumulator: J1.pin2
  N1: J1_2.pin1, S1.O
  N2: J1_2.pin2, S1.P
  N3: J1_2.pin3, S2.O
  N4: J1_2.pin4, S2.P
  Stop 1: S3.Pin_1
  Masa Manetki: S3.Pin_3
  Stop 2: S4.Pin_3

notes:
  G1
  G2
  G3
  G4
  3
  1
  6
  8
  2
