# Fritzing sketch Środek (saved by Fritzing 0.9.3b)
breadboards: 1

parts:
  U1 = PCF8574 [package="DIP16 [THT]"]
  R1 = Resistor [tolerance=±5% resistance=220 package=THT]
  C1 = Ceramic Capacitor [capacitance=100nF package="100 mil [THT, multilayer]"]
  D1 = Schottky Diode [package="300 mil [THT]"]
  R2 = Resistor [tolerance=±5% resistance=220 package=THT]
  R3 = Resistor [tolerance=±5% resistance=220 package=THT]
  R4 = Resistor [tolerance=±5% resistance=220 package=THT]
  R5 = Resistor [tolerance=±5% resistance=220 package=THT]
  R6 = Resistor [tolerance=±5% resistance=220 package=THT]
  R7 = Resistor [tolerance=±5% resistance=10k package=THT]
  R8 = Resistor [tolerance=±5% resistance=10k package=THT]
  R9 = Resistor [tolerance=±5% resistance=10k package=THT]
  C2 = Ceramic Capacitor [capacitance=100nF package="100 mil [THT, multilayer]"]
  C3 = Ceramic Capacitor [capacitance=100nF package="100 mil [THT, multilayer]"]
  R10 = Resistor [tolerance=±5% resistance=220 package=THT]
  C4 = Ceramic Capacitor [capacitance=100nF package="100 mil [THT, multilayer]"]
  C5 = Ceramic Capacitor [capacitance=100nF package="100 mil [THT, multilayer]"]
  C6 = Ceramic Capacitor [capacitance=100nF package="100 mil [THT, multilayer]"]
  C7 = Ceramic Capacitor [capacitance=100nF package="100 mil [THT, multilayer]"]
  R11 = Resistor [tolerance=±5% resistance=10k package=THT]
  R12 = Resistor [tolerance=±5% resistance=10k package=THT]
  R13 = Resistor [tolerance=±5% resistance=10k package=THT]
  R14 = Resistor [tolerance=±5% resistance=10k package=THT]
  LM1 = LM393 [chip_label="LM 393"]
  R15 = Slide Potentiometer [maximum_resistance=100kΩ]
  R16 = Slide Potentiometer [maximum_resistance=100kΩ]
  R17 = Resistor [tolerance=±5% resistance=100k package=THT]
  R18 = Resistor [tolerance=±5% resistance=100k package=THT]
  R19 = Resistor [tolerance=±5% resistance=100k package=THT]
  R20 = Resistor [tolerance=±5% resistance=100k package=THT]
  R21 = Resistor [tolerance=±5% resistance=10k package=THT]
  Part1 = Bluetooth HC-05 Macho [part_number="HC 05"]
  L1 = Inductor [package="400 mil [THT]"]
  C8 = Ceramic Capacitor [capacitance=100nF package="100 mil [THT, multilayer]"]
  C9 = Electrolytic Capacitor [capacitance=1µF package="100 mil [THT, electrolytic]"]
  R22 = Resistor [tolerance=±5% resistance=4.7k package=THT]
  R23 = Resistor [tolerance=±5% resistance=10k package=THT]

nets:
  0V: U1.A0, U1.A1, U1.A3, U1.GND, C1.1, D1.cathode, C2.1, C3.1, C4.1, C5.1, C6.1, C7.1, LM1.connector7, R15.leg1, R16.leg1, R18.Pin_1, Part1.GND, C8.1, C9.-, R23.Pin_0
  N1: U1.P1, R1.Pin_1, C1.0, R7.Pin_1
  N2: U1.P2, R2.Pin_1, R8.Pin_1, C3.0
  N3: U1.P3, R3.Pin_1, R9.Pin_1, C2.0
  N4: U1.P4, R4.Pin_0, C7.0, R11.Pin_0
  N5: U1.P5, R5.Pin_0, C6.0, R12.Pin_0
  N6: U1.P6, R6.Pin_0, C5.0, R13.Pin_0
  N7: U1.P7, R10.Pin_0, C4.0, R14.Pin_0
  SCL: U1.SCL
  SDA: U1.SDA
  5V: U1.VCC, R7.Pin_0, R8.Pin_0, R9.Pin_0, R11.Pin_1, R12.Pin_1, R13.Pin_1, R14.Pin_1, LM1.connector6, R15.leg2, R16.leg2, R21.Pin_0
  Manetka lewy migacz: R1.Pin_0
  Masa manetki: D1.anode
  Manetka prawy migacz: R2.Pin_0
  Manetka swiatlo kierunkowe: R3.Pin_0
  Manetka swiatlo drogowe: R4.Pin_1
  Manetka blinda: R5.Pin_1
  Stop 2: R6.Pin_1
  Stop 1: R10.Pin_1
  N8: LM1.connector0, R21.Pin_1
  Czujnik odbicia TCRT 5000 Magneto: LM1.connector1
  N9: LM1.connector2, R16.wiper
  2: LM1.connector3, R19.Pin_0
  N10: LM1.connector4, R18.Pin_0, R19.Pin_1, R20.Pin_0
  N11: LM1.connector5, R17.Pin_0
  N12: R15.wiper, R17.Pin_1
  Hallotron prędkościomierz: R20.Pin_1
  N13: Part1.TXD, R22.Pin_0, R23.Pin_1
  RX: Part1.RXD
  N14: Part1.VCC, L1.pin_1, C9.+
  3.3V: L1.pin_0, C8.0
  TX: R22.Pin_1
